// Logisim project Digital_Door_Access_System.circ as structural Verilog: 1 circuit, main circuit main
module main (
  input  A__MSB,
  input  constant,
  input  B,
  input  constant_2,
  input  C,
  input  constant_3,
  input  D__LSB,
  input  constant_4,
  output DENIED,
  output UNLOCK
);

  wire XNOR_2_out, XNOR_3_out, XNOR_4_out, XNOR_out;

  xor XNOR (XNOR_out, A__MSB, constant);
  xor XNOR_2 (XNOR_2_out, B, constant_2);
  xor XNOR_3 (XNOR_3_out, C, constant_3);
  xor XNOR_4 (XNOR_4_out, D__LSB, constant_4);
  and _4_INPUT_AND_GATE (DENIED, XNOR_out, XNOR_2_out, XNOR_3_out, XNOR_4_out);
  not not_1 (UNLOCK, DENIED);

  // Notes on the sheet:
  //   E3
  //   E2
  //   E1
  //   E0
endmodule
