// Logisim project PROJECT FILE [DDCA].circ as structural Verilog: 1 circuit, main circuit main
module main (
  input  T,
  input  V,
  input  E,
  input  N,
  output A
);

  wire and_1_out, not_1_out, or_1_out;

  not not_1 (not_1_out, N);
  or or_1 (or_1_out, V, E);
  and and_1 (and_1_out, or_1_out, not_1_out);
  or or_2 (A, T, and_1_out);
endmodule
